# Fritzing sketch BMP085 Barometric pressure sensor (saved by Fritzing 0.9.2b)
breadboards: 1

parts:
  Bauteil1 = Arduino Uno (Rev3)
  Bauteil2 = Barometric Pressure Sensor - BMP085 Breakout

nets:
  N1: Bauteil1.A4/SDA, Bauteil2.GND
  N2: Bauteil1.A5/SCL, Bauteil2.EOC
  3V3: Bauteil1.3V3, Bauteil2.VCC
  N3: Bauteil1.GND, Bauteil2.SDA
