# Fritzing sketch Infrared Motion Sensor (saved by Fritzing 0.9.2b)
breadboards: 1

parts:
  Bauteil1 = Arduino Uno (Rev3)
  LED1 = LED - 5mm [color="Red (633nm)" package="5 mm [THT]"]
  R1 = Resistor [tolerance=±5% resistance=1k package=THT]
  U1 = PIR Sensor HC-SR501

nets:
  N1: Bauteil1.D13/SCK, LED1.anode
  N2: Bauteil1.D2, U1.OUT
  5V: Bauteil1.5V, U1.VCC
  GND: Bauteil1.GND, R1.Pin_0, U1.GND
  N3: LED1.cathode, R1.Pin_1

custom parts:
  PIR Sensor HC-SR501: Passive Infra-Red (PIR) sensor HC-SR501
