# Fritzing sketch photo resistor (saved by Fritzing 0.9.2b)
breadboards: 1

parts:
  Bauteil1 = Arduino Uno (Rev3)
  R1 = Photocell (LDR) [package=THT]
  R2 = Resistor [tolerance=±5% resistance=220 package=THT]

nets:
  N1: Bauteil1.A0, R1.pin_0, R2.Pin_1
  N2: Bauteil1.5V, R2.Pin_0
  N3: Bauteil1.GND, R1.pin_1
