# Fritzing sketch temperature and humidity (saved by Fritzing 0.9.2b)
breadboards: 1

parts:
  Bauteil1 = Arduino Uno (Rev3)
  RHT1 = Humidity and Temperature Sensor RHT03
  R1 = Resistor [tolerance=±5% resistance=1k package=THT]

nets:
  N1: Bauteil1.D2, RHT1.Data-signal, R1.Pin_0
  5V: Bauteil1.5V, RHT1.Vcc, R1.Pin_1
  N2: Bauteil1.GND, RHT1.GND_2
